// Logisim project MCU.circ as structural Verilog: 6 circuits, main circuit MCU
module local_test (
  input  [4:0] in_1,
  input  in_2,
  input  in_3,
  input  in_4,
  input  in_5,
  input  [1:0] in_6,
  input  in_7,
  input  [5:0] in_8
);

  wire clock_1_out, pointer_controller_1_err, pointer_controller_1_ready;
  wire [7:0] field_cahce_1_p1_row_1, field_cahce_1_p1_row_2, field_cahce_1_p1_row_3, field_cahce_1_p1_row_4,
       field_cahce_1_p1_row_5, field_cahce_1_p1_row_6, field_cahce_1_p1_row_7, field_cahce_1_p1_row_8,
       pointer_controller_1_csc, pointer_controller_1_csr;
  wire [8:0] field_cahce_1_p2_row_1, field_cahce_1_p2_row_2, field_cahce_1_p2_row_3, field_cahce_1_p2_row_4,
       field_cahce_1_p2_row_5, field_cahce_1_p2_row_6, field_cahce_1_p2_row_7, field_cahce_1_p2_row_8;
  wire [9:0] field_cahce_1_task_row_1, field_cahce_1_task_row_2, field_cahce_1_task_row_3,
       field_cahce_1_task_row_4, field_cahce_1_task_row_5, field_cahce_1_task_row_6,
       field_cahce_1_task_row_7, field_cahce_1_task_row_8;
  wire [31:0] field_cahce_1_datao_1, field_cahce_1_datao_2;

  Clock clock_1 (.out(clock_1_out));
  DotMatrix #(.inputtype("row"), .matrixcols(9), .matrixrows(8)) dotmatrix_1 (
    .row0(field_cahce_1_p2_row_1), .row1(field_cahce_1_p2_row_2), .row2(field_cahce_1_p2_row_3),
    .row3(field_cahce_1_p2_row_4), .row4(field_cahce_1_p2_row_5), .row5(field_cahce_1_p2_row_6),
    .row6(field_cahce_1_p2_row_7), .row7(field_cahce_1_p2_row_8));
  DotMatrix #(.inputtype("row"), .matrixcols(8), .matrixrows(8)) dotmatrix_2 (
    .row0(field_cahce_1_p1_row_1), .row1(field_cahce_1_p1_row_2), .row2(field_cahce_1_p1_row_3),
    .row3(field_cahce_1_p1_row_4), .row4(field_cahce_1_p1_row_5), .row5(field_cahce_1_p1_row_6),
    .row6(field_cahce_1_p1_row_7), .row7(field_cahce_1_p1_row_8));
  DotMatrix #(.inputtype("row"), .matrixcols(10), .matrixrows(8), .dotshape("circle")) dotmatrix_3 (
    .row0(field_cahce_1_task_row_1), .row1(field_cahce_1_task_row_2), .row2(field_cahce_1_task_row_3),
    .row3(field_cahce_1_task_row_4), .row4(field_cahce_1_task_row_5), .row5(field_cahce_1_task_row_6),
    .row6(field_cahce_1_task_row_7), .row7(field_cahce_1_task_row_8));
  Field_cahce field_cahce_1 (
    .Task_row_1(field_cahce_1_task_row_1), .p2_row_1(field_cahce_1_p2_row_1),
    .Task_row_2(field_cahce_1_task_row_2), .p2_row_2(field_cahce_1_p2_row_2),
    .p1_row_1(field_cahce_1_p1_row_1), .p1_row_2(field_cahce_1_p1_row_2),
    .Task_row_3(field_cahce_1_task_row_3), .p2_row_3(field_cahce_1_p2_row_3),
    .p1_row_3(field_cahce_1_p1_row_3), .Task_row_4(field_cahce_1_task_row_4),
    .p2_row_4(field_cahce_1_p2_row_4), .p1_row_4(field_cahce_1_p1_row_4),
    .Task_row_5(field_cahce_1_task_row_5), .p2_row_5(field_cahce_1_p2_row_5),
    .p1_row_5(field_cahce_1_p1_row_5), .Task_row_6(field_cahce_1_task_row_6),
    .p2_row_6(field_cahce_1_p2_row_6), .p1_row_6(field_cahce_1_p1_row_6), .p1_row_7(field_cahce_1_p1_row_7),
    .Task_row_7(field_cahce_1_task_row_7), .p2_row_7(field_cahce_1_p2_row_7),
    .p1_row_8(field_cahce_1_p1_row_8), .Task_row_8(field_cahce_1_task_row_8),
    .p2_row_8(field_cahce_1_p2_row_8), .wr(in_7), .DataI(in_8), .RST(in_2), .p_sel(in_6),
    .DataO_1(field_cahce_1_datao_1), .DataO_2(field_cahce_1_datao_2));
  pointer_controller pointer_controller_1 (
    .Active(in_3), .CLK(clock_1_out), .RST(in_2), .Field_state_1(field_cahce_1_datao_1),
    .Field_state_2(field_cahce_1_datao_2), .Free_mode(in_5), .CSC(pointer_controller_1_csc),
    .CSR(pointer_controller_1_csr), .Err(pointer_controller_1_err), .Ready(pointer_controller_1_ready),
    .KBD_command(in_1), .Allow_nearby(in_4));
  LED led_1 (.in(pointer_controller_1_err));
  // Probe on pointer_controller_1_csc
  LED led_2 (.in(pointer_controller_1_ready));
  // Probe on pointer_controller_1_csr
  // DotMatrix #(.inputtype("select"), .matrixcols(8), .matrixrows(8)) dotmatrix_4: pin names not known; wires that end beside it: pointer_controller_1_csc
endmodule

module MCU (
  input  [4:0] KBD_command,
  input  [10:0] KBD_energy_increment,
  input  KBD_Ready,
  input  Reset,
  input  CLK,
  input  MISO,
  input  SPI_busy,
  output Request_KBD,
  output Request_KBD_energy,
  output [7:0] Cell_CSC,
  output [7:0] Cell_CSR,
  output [2:0] Table_CSC,
  output [5:0] Table_CSR,
  output Task_CS,
  output SPI_clock,
  output MOSI,
  output [7:0] Debug_out,
  output Waiting_IO,
  output SPI_communication_in_progress
);

  wire and_1_out, and_2_out, and_3_out, and_4_out, and_5_out, and_6_out, and_7_out, and_8_out, and_10_out,
       and_11_out, cdm_8_1_data_code_prime, cdm_8_1_load_st_prime, cdm_8_1_mem, d_ff_1_q, Data,
       decoder_1_out0, io_dmx_1_cell_csc, io_dmx_1_cell_csr, io_dmx_1_debug_output, io_dmx_1_is_io,
       io_dmx_1_spi_kbd_control, io_dmx_1_table__csc__csr____task_cs, io_dmx_1_universal_io_1,
       io_dmx_1_universal_io_2, not_1_out, or_1_out, or_2_out, or_3_out, or_5_out,
       spi_module_master_1_communication_end, spi_module_master_1_input_transanction_end,
       spi_module_master_1_output_transanction_end;
  wire [6:0] demultiplexer_2_out0, demultiplexer_2_out1, register_4_q;
  wire [6:3] register_3_q;
  wire [7:0] cdm_8_1_addr, cdm_8_1_data_out, cdm_8_1_pc, cdm_8_1_ps, cdm_8_1_r0, cdm_8_1_r1, cdm_8_1_r2,
       cdm_8_1_r3, cdm_8_1_sp, controlled_buffer_1_out, controlled_buffer_2_out, controlled_buffer_4_out,
       controlled_buffer_6_out, register_5_q, register_6_q;
  wire [15:0] spi_module_master_1_recv_data;

  // Probe on cdm_8_1_r0
  // Probe on cdm_8_1_r0
  // Probe on cdm_8_1_r0
  // Probe on cdm_8_1_ps[7]
  // Probe on cdm_8_1_ps[6:4]
  // Probe on cdm_8_1_pc
  // Probe on cdm_8_1_r1
  // Probe on cdm_8_1_r0
  // Probe on cdm_8_1_ps[3]
  // Probe on cdm_8_1_ps[2]
  // Probe on cdm_8_1_r1
  // Probe on cdm_8_1_r1
  // Probe on cdm_8_1_r1
  // Probe on cdm_8_1_ps[1]
  // Probe on cdm_8_1_ps[0]
  // Probe on cdm_8_1_r2
  // Probe on cdm_8_1_r2
  // Probe on cdm_8_1_r2
  // Probe on cdm_8_1_r2
  // Probe on cdm_8_1_sp
  // Probe on cdm_8_1_r3
  // Probe on cdm_8_1_r3
  and and_1 (and_1_out, CLK, ~Waiting_IO);  // AND_Gate
  // Probe on cdm_8_1_r3
  // Probe on cdm_8_1_r3
  CdM_8 cdm_8_1 (
    .data_code_prime(cdm_8_1_data_code_prime), .R0(cdm_8_1_r0), .R1(cdm_8_1_r1), .mem(cdm_8_1_mem),
    .R2(cdm_8_1_r2), .load_st_prime(cdm_8_1_load_st_prime), .R3(cdm_8_1_r3), .addr(cdm_8_1_addr),
    .PC(cdm_8_1_pc), .SP(cdm_8_1_sp), .data_out(cdm_8_1_data_out), .data_in(controlled_buffer_2_out),
    .PS(cdm_8_1_ps), .clk(and_1_out), .rset(Reset));  // open: page, IAck, IRQ, vector, shadow
  Decoder #(.disabled(0)) decoder_1 (
    .out0(decoder_1_out0), .out1(Data), .sel(cdm_8_1_data_code_prime), .en(cdm_8_1_mem));
  assign controlled_buffer_1_out = not_1_out ? cdm_8_1_data_out : 8'bz;  // Controlled_Buffer controlled_buffer_1
  not not_1 (not_1_out, cdm_8_1_load_st_prime);
  assign controlled_buffer_2_out = cdm_8_1_load_st_prime ? controlled_buffer_1_out : 8'bz;  // Controlled_Buffer controlled_buffer_2
  and and_2 (and_2_out, ~io_dmx_1_is_io, Data);  // AND_Gate
  IO_dmx io_dmx_1 (
    .Address(cdm_8_1_addr), .Is_IO(io_dmx_1_is_io), .Cell_CSC(io_dmx_1_cell_csc),
    .Cell_CSR(io_dmx_1_cell_csr), .Table__CSC__CSR____Task_CS(io_dmx_1_table__csc__csr____task_cs),
    .SPI_KBD_control(io_dmx_1_spi_kbd_control), .Universal_IO_1(io_dmx_1_universal_io_1),
    .Universal_IO_2(io_dmx_1_universal_io_2), .Debug_output(io_dmx_1_debug_output), .Selected(Data));
  ROM rom_1 (.addr(cdm_8_1_addr), .data(controlled_buffer_1_out), .sel(decoder_1_out0));
  RAM ram_1 (
    .addr(cdm_8_1_addr), .data(controlled_buffer_1_out), .sel(and_2_out), .clk(CLK),
    .ld(cdm_8_1_load_st_prime), .clr(Reset));
  and and_3 (and_3_out, io_dmx_1_is_io, ~cdm_8_1_load_st_prime, io_dmx_1_universal_io_1);  // AND_Gate
  or or_1 (or_1_out, io_dmx_1_universal_io_1, spi_module_master_1_communication_end, and_11_out);
  and and_4 (and_4_out, io_dmx_1_is_io, ~cdm_8_1_load_st_prime, io_dmx_1_universal_io_2);  // AND_Gate
  or or_2 (or_2_out, io_dmx_1_universal_io_2, spi_module_master_1_communication_end, and_11_out);
  Register #(.trigger("falling")) register_1 (
    .D(controlled_buffer_1_out), .en(io_dmx_1_cell_csc), .Q(Cell_CSC), .clk(CLK), .clr(Reset));
  Register #(.trigger("falling")) register_2 (
    .D(controlled_buffer_1_out), .en(io_dmx_1_cell_csr), .Q(Cell_CSR), .clk(CLK), .clr(Reset));
  Register #(.trigger("falling")) register_3 (
    .D(controlled_buffer_1_out), .en(io_dmx_1_table__csc__csr____task_cs),
    .Q({Task_CS, register_3_q, Table_CSC}), .clk(CLK), .clr(Reset));
  Register #(.trigger("falling")) register_4 (
    .D(controlled_buffer_1_out), .en(io_dmx_1_spi_kbd_control), .Q({Request_KBD, register_4_q}), .clk(CLK),
    .clr(or_3_out));
  and and_5 (and_5_out, io_dmx_1_is_io, cdm_8_1_load_st_prime, io_dmx_1_universal_io_1);
  assign controlled_buffer_1_out = and_5_out ? register_5_q : 8'bz;  // Controlled_Buffer controlled_buffer_3
  Register #(.trigger("falling")) register_5 (
    .D(controlled_buffer_4_out), .en(or_1_out), .Q(register_5_q), .clk(CLK), .clr(Reset));
  assign controlled_buffer_4_out = and_3_out ? controlled_buffer_1_out : 8'bz;  // Controlled_Buffer controlled_buffer_4
  and and_6 (and_6_out, io_dmx_1_is_io, io_dmx_1_universal_io_2, cdm_8_1_load_st_prime);
  assign controlled_buffer_1_out = and_6_out ? register_6_q : 8'bz;  // Controlled_Buffer controlled_buffer_5
  Register #(.trigger("falling")) register_6 (
    .D(controlled_buffer_6_out), .en(or_2_out), .Q(register_6_q), .clk(CLK), .clr(Reset));
  assign controlled_buffer_6_out = and_4_out ? controlled_buffer_1_out : 8'bz;  // Controlled_Buffer controlled_buffer_6
  Register #(.trigger("falling")) register_7 (
    .D(controlled_buffer_1_out), .en(io_dmx_1_debug_output), .Q(Debug_out), .clk(CLK), .clr(Reset));
  Demultiplexer #(.width(3), .disabled(0), .enable("false")) demultiplexer_1 (
    .out0(Table_CSR[2:0]), .out1(Table_CSR[5:3]), .in(register_3_q[5:3]), .sel(register_3_q[6]));
  Demultiplexer #(.width(7), .disabled(0), .enable("false")) demultiplexer_2 (
    .out0(demultiplexer_2_out0), .out1(demultiplexer_2_out1), .in(register_4_q), .sel(Request_KBD));
  or or_3 (or_3_out, and_7_out, Reset);
  and and_7 (and_7_out, Waiting_IO, or_5_out, and_8_out);
  D_Flip_Flop d_ff_1 (.clk(CLK), .D(CLK), .Q(d_ff_1_q), .reset(and_8_out));  // open: Qn, preset, en
  or or_4 (Waiting_IO, Request_KBD, SPI_communication_in_progress);
  or or_5 (or_5_out, and_11_out, spi_module_master_1_communication_end);
  and and_8 (and_8_out, ~CLK, d_ff_1_q);  // AND_Gate
  or or_6 (SPI_communication_in_progress, demultiplexer_2_out0[6], demultiplexer_2_out0[5], demultiplexer_2_out0[4], demultiplexer_2_out0[3], demultiplexer_2_out0[2], demultiplexer_2_out0[1], demultiplexer_2_out0[0]);
  and and_9 (Request_KBD_energy, demultiplexer_2_out1[0], Request_KBD);
  Pull_Resistor pull_resistor_1 (.node(SPI_busy));
  assign {controlled_buffer_6_out, controlled_buffer_4_out} = and_11_out ? {KBD_energy_increment, KBD_command} : 16'bz;  // Controlled_Buffer controlled_buffer_7
  assign {controlled_buffer_6_out, controlled_buffer_4_out} = spi_module_master_1_communication_end ? spi_module_master_1_recv_data : 16'bz;  // Controlled_Buffer controlled_buffer_8
  and and_10 (and_10_out, CLK, SPI_communication_in_progress, ~SPI_busy);  // AND_Gate
  LED led_1 (.in(spi_module_master_1_input_transanction_end));
  SPI_module__master spi_module_master_1 (
    .In_clock(and_10_out), .MISO(MISO), .CLK(SPI_clock), .MOSI(MOSI),
    .Output_transanction_end(spi_module_master_1_output_transanction_end),
    .Input_transanction_end(spi_module_master_1_input_transanction_end),
    .Control_command({Request_KBD, register_4_q}), .Send_command(register_5_q[4:0]),
    .Send_energy({register_6_q, register_5_q[7:5]}), .Recv_data(spi_module_master_1_recv_data),
    .Communication_end(spi_module_master_1_communication_end));
  LED led_2 (.in(spi_module_master_1_communication_end));
  LED led_3 (.in(spi_module_master_1_output_transanction_end));
  and and_11 (and_11_out, Request_KBD, KBD_Ready);
  Pull_Resistor pull_resistor_2 (.node(MISO));

  // Other names for the same wires on the sheet: wait_KBD = Request_KBD; wait_IO = Waiting_IO;
  //   wait_SPI = SPI_communication_in_progress

  // Notes on the sheet:
  //   contents of rom_1 (hex, n*v repeats v):
  //   d0 f9 d1 ff a1 d0 ff d1 ff a1 88 a1 d0 fc d1 2e a1 d0 fb d1 10 a1 d0 fc d1 c a1 d0 f9 d1 0 a1 d0 ff
  //   d1 0 a1 88 a1 d0 ea d1 1 a1 d2 ff a9 88 a1 8a a9 d0 fc d1 26 a1 d0 fc d1 80 a1 d0 fb b1 d0 10 71 e1
  //   55 0 d0 f9 d1 18 a1 d0 e9 b1 9d a1 d0 fe a1 ee 33 d0 11 71 e1 6a 0 d0 f9 d1 3 a1 d0 ea b1 9d a1 d0
  //   ff a1 ee 33 d0 12 71 e1 82 0 d0 f9 d1 c0 a1 d0 ea b1 91 e3 7c 91 a1 d0 ff a1 ee 33 d0 13 71 e1 9a 0
  //   d0 f9 d1 24 a1 d0 e9 b1 91 e3 94 91 a1 d0 fe a1 ee 33 d0 8 71 e1 d7 d0 ff d1 0 a1 d2 ea b9 a1 d0 fc
  //   d1 2e a1 d0 f9 d1 42 a1 d0 fc d1 81 a1 d0 fb b1 d2 8 56 a2 d0 fc d1 4 a1 d0 fb b1 d0 f9 d2 d0 56 a2
  //   d0 ff d1 0 a1 d2 ea b9 a1 ee 33 d0 f9 d1 c3 a1 d1 0 d0 ff a1 d0 ea b1 d0 ff a1 ee 33
endmodule

module IO_dmx (
  input  [7:0] Address,
  input  Selected,
  output Is_IO,
  output Cell_CSC,
  output Cell_CSR,
  output Table__CSC__CSR____Task_CS,
  output SPI_KBD_control,
  output Universal_IO_1,
  output Universal_IO_2,
  output Debug_output
);

  wire [7:0] pull_resistor_1_node;

  Pull_Resistor pull_resistor_1 (.node(pull_resistor_1_node));
  assign pull_resistor_1_node = Selected ? Address : 8'bz;  // Controlled_Buffer controlled_buffer_1
  Comparator comparator_1 (.a(pull_resistor_1_node), .b({8{1'b1}}), .eq(Cell_CSC));  // open: gt, lt
  Comparator comparator_2 (.a(pull_resistor_1_node), .b(8'hfe), .eq(Cell_CSR));  // open: gt, lt
  Comparator comparator_3 (.a(pull_resistor_1_node), .b(8'hfd), .eq(Table__CSC__CSR____Task_CS));  // open: gt, lt
  Comparator comparator_4 (.a(pull_resistor_1_node), .b(8'hfc), .eq(SPI_KBD_control));  // open: gt, lt
  Comparator comparator_5 (.a(pull_resistor_1_node), .b(8'hfb), .eq(Universal_IO_1));  // open: gt, lt
  Comparator comparator_6 (.a(pull_resistor_1_node), .b(8'hfa), .eq(Universal_IO_2));  // open: gt, lt
  Comparator comparator_7 (.a(pull_resistor_1_node), .b(8'hf9), .eq(Debug_output));  // open: gt, lt
  or or_1 (Is_IO, Cell_CSC, Cell_CSR, Table__CSC__CSR____Task_CS, SPI_KBD_control, Universal_IO_1, Universal_IO_2, Debug_output);
endmodule

module Field_cahce (
  input  wr,
  input  [5:0] DataI,
  input  RST,
  input  [1:0] p_sel,
  output [9:0] Task_row_1,
  output [8:0] p2_row_1,
  output [9:0] Task_row_2,
  output [8:0] p2_row_2,
  output [7:0] p1_row_1,
  output [31:0] DataO_1,
  output [31:0] DataO_2,
  output [7:0] p1_row_2,
  output [7:0] p1_row_3,
  output [8:0] p2_row_3,
  output [9:0] Task_row_3,
  output [7:0] p1_row_4,
  output [8:0] p2_row_4,
  output [9:0] Task_row_4,
  output [9:0] Task_row_5,
  output [8:0] p2_row_5,
  output [9:0] Task_row_6,
  output [7:0] p1_row_5,
  output [8:0] p2_row_6,
  output [7:0] p1_row_6,
  output [7:0] p1_row_7,
  output [7:0] p1_row_8,
  output [8:0] p2_row_7,
  output [9:0] Task_row_7,
  output [8:0] p2_row_8,
  output [9:0] Task_row_8
);

  wire decoder_2_out0, decoder_2_out1, decoder_2_out2, decoder_2_out3, or_1_out, or_4_out, or_7_out,
       or_8_out, or_9_out, or_12_out;
  wire [7:0] decoder_1_out0, demultiplexer_1_out0, demultiplexer_1_out1, demultiplexer_2_out0,
       demultiplexer_2_out1, demultiplexer_2_out2, demultiplexer_2_out3, demultiplexer_3_out0,
       demultiplexer_3_out1, demultiplexer_3_out2, demultiplexer_3_out3;
  wire [31:0] and_1_out, and_2_out, and_3_out, and_4_out, and_5_out, and_6_out, multiplexer_1_out,
       multiplexer_2_out, multiplexer_3_out, multiplexer_4_out, multiplexer_5_out, multiplexer_6_out,
       or_2_out, or_3_out, or_5_out, or_6_out, or_10_out, or_11_out;

  Decoder #(.select(3), .enable("false")) decoder_1 (
    .out0(decoder_1_out0[0]), .out1(decoder_1_out0[1]), .out2(decoder_1_out0[2]), .out3(decoder_1_out0[3]),
    .out4(decoder_1_out0[4]), .out5(decoder_1_out0[5]), .out6(decoder_1_out0[6]), .out7(decoder_1_out0[7]),
    .sel(DataI[5:3]));
  Demultiplexer #(.width(8), .enable("false")) demultiplexer_1 (
    .out0(demultiplexer_1_out0), .out1(demultiplexer_1_out1), .in(decoder_1_out0), .sel(DataI[2]));
  Pull_Resistor pull_resistor_1 (.node(DataI));
  Demultiplexer #(.select(2), .width(8), .enable("false")) demultiplexer_2 (
    .out0(demultiplexer_2_out0), .out1(demultiplexer_2_out1), .out2(demultiplexer_2_out2),
    .out3(demultiplexer_2_out3), .in(demultiplexer_1_out0), .sel(DataI[1:0]));
  Demultiplexer #(.select(2), .width(8), .enable("false")) demultiplexer_3 (
    .out0(demultiplexer_3_out0), .out1(demultiplexer_3_out1), .out2(demultiplexer_3_out2),
    .out3(demultiplexer_3_out3), .in(demultiplexer_1_out1), .sel(DataI[1:0]));
  Pull_Resistor pull_resistor_2 (.node(p_sel));
  Decoder #(.select(2), .disabled(0), .enable("false")) decoder_2 (
    .out0(decoder_2_out0), .out1(decoder_2_out1), .out2(decoder_2_out2), .out3(decoder_2_out3), .sel(p_sel));
  or or_1 (or_1_out, decoder_2_out0, decoder_2_out1);
  Multiplexer #(.width(32), .enable("false")) multiplexer_1 (
    .in0(or_2_out), .in1(and_1_out), .out(multiplexer_1_out), .sel(decoder_2_out0));
  assign and_1_out = ~{demultiplexer_2_out3, demultiplexer_2_out2, demultiplexer_2_out1, demultiplexer_2_out0} & {p1_row_4[0], p1_row_4[1], p1_row_4[2], p1_row_4[3], p1_row_4[4], p1_row_4[5], p1_row_4[6], p1_row_4[7], p1_row_3[0], p1_row_3[1], p1_row_3[2], p1_row_3[3], p1_row_3[4], p1_row_3[5], p1_row_3[6], p1_row_3[7], p1_row_2[0], p1_row_2[1], p1_row_2[2], p1_row_2[3], p1_row_2[4], p1_row_2[5], p1_row_2[6], p1_row_2[7], p1_row_1[0], p1_row_1[1], p1_row_1[2], p1_row_1[3], p1_row_1[4], p1_row_1[5], p1_row_1[6], p1_row_1[7]};  // AND_Gate and_1, 32 bits wide
  assign or_2_out = {demultiplexer_2_out3, demultiplexer_2_out2, demultiplexer_2_out1, demultiplexer_2_out0} | {p1_row_4[0], p1_row_4[1], p1_row_4[2], p1_row_4[3], p1_row_4[4], p1_row_4[5], p1_row_4[6], p1_row_4[7], p1_row_3[0], p1_row_3[1], p1_row_3[2], p1_row_3[3], p1_row_3[4], p1_row_3[5], p1_row_3[6], p1_row_3[7], p1_row_2[0], p1_row_2[1], p1_row_2[2], p1_row_2[3], p1_row_2[4], p1_row_2[5], p1_row_2[6], p1_row_2[7], p1_row_1[0], p1_row_1[1], p1_row_1[2], p1_row_1[3], p1_row_1[4], p1_row_1[5], p1_row_1[6], p1_row_1[7]};  // OR_Gate or_2, 32 bits wide
  assign or_3_out = {demultiplexer_3_out3, demultiplexer_3_out2, demultiplexer_3_out1, demultiplexer_3_out0} | {p1_row_8[0], p1_row_8[1], p1_row_8[2], p1_row_8[3], p1_row_8[4], p1_row_8[5], p1_row_8[6], p1_row_8[7], p1_row_7[0], p1_row_7[1], p1_row_7[2], p1_row_7[3], p1_row_7[4], p1_row_7[5], p1_row_7[6], p1_row_7[7], p1_row_6[0], p1_row_6[1], p1_row_6[2], p1_row_6[3], p1_row_6[4], p1_row_6[5], p1_row_6[6], p1_row_6[7], p1_row_5[0], p1_row_5[1], p1_row_5[2], p1_row_5[3], p1_row_5[4], p1_row_5[5], p1_row_5[6], p1_row_5[7]};  // OR_Gate or_3, 32 bits wide
  Multiplexer #(.width(32), .enable("false")) multiplexer_2 (
    .in0(or_3_out), .in1(and_2_out), .out(multiplexer_2_out), .sel(decoder_2_out0));
  or or_4 (or_4_out, decoder_2_out0, decoder_2_out1);
  assign DataO_1 = decoder_2_out1 ? {p1_row_4[0], p1_row_4[1], p1_row_4[2], p1_row_4[3], p1_row_4[4], p1_row_4[5], p1_row_4[6], p1_row_4[7], p1_row_3[0], p1_row_3[1], p1_row_3[2], p1_row_3[3], p1_row_3[4], p1_row_3[5], p1_row_3[6], p1_row_3[7], p1_row_2[0], p1_row_2[1], p1_row_2[2], p1_row_2[3], p1_row_2[4], p1_row_2[5], p1_row_2[6], p1_row_2[7], p1_row_1[0], p1_row_1[1], p1_row_1[2], p1_row_1[3], p1_row_1[4], p1_row_1[5], p1_row_1[6], p1_row_1[7]} : 32'bz;  // Controlled_Buffer controlled_buffer_1
  Register #(.width(32)) register_1 (
    .D(multiplexer_1_out), .en(or_1_out),
    .Q({p1_row_4[0], p1_row_4[1], p1_row_4[2], p1_row_4[3], p1_row_4[4], p1_row_4[5], p1_row_4[6], p1_row_4[7], p1_row_3[0], p1_row_3[1], p1_row_3[2], p1_row_3[3], p1_row_3[4], p1_row_3[5], p1_row_3[6], p1_row_3[7], p1_row_2[0], p1_row_2[1], p1_row_2[2], p1_row_2[3], p1_row_2[4], p1_row_2[5], p1_row_2[6], p1_row_2[7], p1_row_1[0], p1_row_1[1], p1_row_1[2], p1_row_1[3], p1_row_1[4], p1_row_1[5], p1_row_1[6], p1_row_1[7]}),
    .clk(wr), .clr(RST));
  assign or_5_out = {demultiplexer_2_out3, demultiplexer_2_out2, demultiplexer_2_out1, demultiplexer_2_out0} | {p2_row_4[0], p2_row_4[1], p2_row_4[2], p2_row_4[3], p2_row_4[4], p2_row_4[5], p2_row_4[6], p2_row_4[7], p2_row_3[0], p2_row_3[1], p2_row_3[2], p2_row_3[3], p2_row_3[4], p2_row_3[5], p2_row_3[6], p2_row_3[7], p2_row_2[0], p2_row_2[1], p2_row_2[2], p2_row_2[3], p2_row_2[4], p2_row_2[5], p2_row_2[6], p2_row_2[7], p2_row_1[0], p2_row_1[1], p2_row_1[2], p2_row_1[3], p2_row_1[4], p2_row_1[5], p2_row_1[6], p2_row_1[7]};  // OR_Gate or_5, 32 bits wide
  assign or_6_out = {demultiplexer_3_out3, demultiplexer_3_out2, demultiplexer_3_out1, demultiplexer_3_out0} | {p2_row_8[0], p2_row_8[1], p2_row_8[2], p2_row_8[3], p2_row_8[4], p2_row_8[5], p2_row_8[6], p2_row_8[7], p2_row_7[0], p2_row_7[1], p2_row_7[2], p2_row_7[3], p2_row_7[4], p2_row_7[5], p2_row_7[6], p2_row_7[7], p2_row_6[0], p2_row_6[1], p2_row_6[2], p2_row_6[3], p2_row_6[4], p2_row_6[5], p2_row_6[6], p2_row_6[7], p2_row_5[0], p2_row_5[1], p2_row_5[2], p2_row_5[3], p2_row_5[4], p2_row_5[5], p2_row_5[6], p2_row_5[7]};  // OR_Gate or_6, 32 bits wide
  assign and_2_out = ~{demultiplexer_3_out3, demultiplexer_3_out2, demultiplexer_3_out1, demultiplexer_3_out0} & {p1_row_8[0], p1_row_8[1], p1_row_8[2], p1_row_8[3], p1_row_8[4], p1_row_8[5], p1_row_8[6], p1_row_8[7], p1_row_7[0], p1_row_7[1], p1_row_7[2], p1_row_7[3], p1_row_7[4], p1_row_7[5], p1_row_7[6], p1_row_7[7], p1_row_6[0], p1_row_6[1], p1_row_6[2], p1_row_6[3], p1_row_6[4], p1_row_6[5], p1_row_6[6], p1_row_6[7], p1_row_5[0], p1_row_5[1], p1_row_5[2], p1_row_5[3], p1_row_5[4], p1_row_5[5], p1_row_5[6], p1_row_5[7]};  // AND_Gate and_2, 32 bits wide
  Register #(.width(32)) register_2 (
    .D(multiplexer_2_out), .en(or_4_out),
    .Q({p1_row_8[0], p1_row_8[1], p1_row_8[2], p1_row_8[3], p1_row_8[4], p1_row_8[5], p1_row_8[6], p1_row_8[7], p1_row_7[0], p1_row_7[1], p1_row_7[2], p1_row_7[3], p1_row_7[4], p1_row_7[5], p1_row_7[6], p1_row_7[7], p1_row_6[0], p1_row_6[1], p1_row_6[2], p1_row_6[3], p1_row_6[4], p1_row_6[5], p1_row_6[6], p1_row_6[7], p1_row_5[0], p1_row_5[1], p1_row_5[2], p1_row_5[3], p1_row_5[4], p1_row_5[5], p1_row_5[6], p1_row_5[7]}),
    .clk(wr), .clr(RST));
  assign DataO_2 = decoder_2_out1 ? {p1_row_8[0], p1_row_8[1], p1_row_8[2], p1_row_8[3], p1_row_8[4], p1_row_8[5], p1_row_8[6], p1_row_8[7], p1_row_7[0], p1_row_7[1], p1_row_7[2], p1_row_7[3], p1_row_7[4], p1_row_7[5], p1_row_7[6], p1_row_7[7], p1_row_6[0], p1_row_6[1], p1_row_6[2], p1_row_6[3], p1_row_6[4], p1_row_6[5], p1_row_6[6], p1_row_6[7], p1_row_5[0], p1_row_5[1], p1_row_5[2], p1_row_5[3], p1_row_5[4], p1_row_5[5], p1_row_5[6], p1_row_5[7]} : 32'bz;  // Controlled_Buffer controlled_buffer_2
  assign DataO_1 = decoder_2_out2 ? {p2_row_4[0], p2_row_4[1], p2_row_4[2], p2_row_4[3], p2_row_4[4], p2_row_4[5], p2_row_4[6], p2_row_4[7], p2_row_3[0], p2_row_3[1], p2_row_3[2], p2_row_3[3], p2_row_3[4], p2_row_3[5], p2_row_3[6], p2_row_3[7], p2_row_2[0], p2_row_2[1], p2_row_2[2], p2_row_2[3], p2_row_2[4], p2_row_2[5], p2_row_2[6], p2_row_2[7], p2_row_1[0], p2_row_1[1], p2_row_1[2], p2_row_1[3], p2_row_1[4], p2_row_1[5], p2_row_1[6], p2_row_1[7]} : 32'bz;  // Controlled_Buffer controlled_buffer_3
  Register #(.width(32)) register_3 (
    .D(multiplexer_3_out), .en(or_7_out),
    .Q({p2_row_4[0], p2_row_4[1], p2_row_4[2], p2_row_4[3], p2_row_4[4], p2_row_4[5], p2_row_4[6], p2_row_4[7], p2_row_3[0], p2_row_3[1], p2_row_3[2], p2_row_3[3], p2_row_3[4], p2_row_3[5], p2_row_3[6], p2_row_3[7], p2_row_2[0], p2_row_2[1], p2_row_2[2], p2_row_2[3], p2_row_2[4], p2_row_2[5], p2_row_2[6], p2_row_2[7], p2_row_1[0], p2_row_1[1], p2_row_1[2], p2_row_1[3], p2_row_1[4], p2_row_1[5], p2_row_1[6], p2_row_1[7]}),
    .clk(wr), .clr(RST));
  or or_7 (or_7_out, decoder_2_out0, decoder_2_out2);
  Multiplexer #(.width(32), .enable("false")) multiplexer_3 (
    .in0(or_5_out), .in1(and_3_out), .out(multiplexer_3_out), .sel(decoder_2_out0));
  assign and_3_out = ~{demultiplexer_2_out3, demultiplexer_2_out2, demultiplexer_2_out1, demultiplexer_2_out0} & {p2_row_4[0], p2_row_4[1], p2_row_4[2], p2_row_4[3], p2_row_4[4], p2_row_4[5], p2_row_4[6], p2_row_4[7], p2_row_3[0], p2_row_3[1], p2_row_3[2], p2_row_3[3], p2_row_3[4], p2_row_3[5], p2_row_3[6], p2_row_3[7], p2_row_2[0], p2_row_2[1], p2_row_2[2], p2_row_2[3], p2_row_2[4], p2_row_2[5], p2_row_2[6], p2_row_2[7], p2_row_1[0], p2_row_1[1], p2_row_1[2], p2_row_1[3], p2_row_1[4], p2_row_1[5], p2_row_1[6], p2_row_1[7]};  // AND_Gate and_3, 32 bits wide
  assign and_4_out = ~{demultiplexer_3_out3, demultiplexer_3_out2, demultiplexer_3_out1, demultiplexer_3_out0} & {p2_row_8[0], p2_row_8[1], p2_row_8[2], p2_row_8[3], p2_row_8[4], p2_row_8[5], p2_row_8[6], p2_row_8[7], p2_row_7[0], p2_row_7[1], p2_row_7[2], p2_row_7[3], p2_row_7[4], p2_row_7[5], p2_row_7[6], p2_row_7[7], p2_row_6[0], p2_row_6[1], p2_row_6[2], p2_row_6[3], p2_row_6[4], p2_row_6[5], p2_row_6[6], p2_row_6[7], p2_row_5[0], p2_row_5[1], p2_row_5[2], p2_row_5[3], p2_row_5[4], p2_row_5[5], p2_row_5[6], p2_row_5[7]};  // AND_Gate and_4, 32 bits wide
  Multiplexer #(.width(32), .enable("false")) multiplexer_4 (
    .in0(or_6_out), .in1(and_4_out), .out(multiplexer_4_out), .sel(decoder_2_out0));
  Register #(.width(32)) register_4 (
    .D(multiplexer_4_out), .en(or_8_out),
    .Q({p2_row_8[0], p2_row_8[1], p2_row_8[2], p2_row_8[3], p2_row_8[4], p2_row_8[5], p2_row_8[6], p2_row_8[7], p2_row_7[0], p2_row_7[1], p2_row_7[2], p2_row_7[3], p2_row_7[4], p2_row_7[5], p2_row_7[6], p2_row_7[7], p2_row_6[0], p2_row_6[1], p2_row_6[2], p2_row_6[3], p2_row_6[4], p2_row_6[5], p2_row_6[6], p2_row_6[7], p2_row_5[0], p2_row_5[1], p2_row_5[2], p2_row_5[3], p2_row_5[4], p2_row_5[5], p2_row_5[6], p2_row_5[7]}),
    .clk(wr), .clr(RST));
  or or_8 (or_8_out, decoder_2_out0, decoder_2_out2);
  assign DataO_2 = decoder_2_out2 ? {p2_row_8[0], p2_row_8[1], p2_row_8[2], p2_row_8[3], p2_row_8[4], p2_row_8[5], p2_row_8[6], p2_row_8[7], p2_row_7[0], p2_row_7[1], p2_row_7[2], p2_row_7[3], p2_row_7[4], p2_row_7[5], p2_row_7[6], p2_row_7[7], p2_row_6[0], p2_row_6[1], p2_row_6[2], p2_row_6[3], p2_row_6[4], p2_row_6[5], p2_row_6[6], p2_row_6[7], p2_row_5[0], p2_row_5[1], p2_row_5[2], p2_row_5[3], p2_row_5[4], p2_row_5[5], p2_row_5[6], p2_row_5[7]} : 32'bz;  // Controlled_Buffer controlled_buffer_4
  or or_9 (or_9_out, decoder_2_out0, decoder_2_out3);
  Multiplexer #(.width(32), .enable("false")) multiplexer_5 (
    .in0(or_10_out), .in1(and_5_out), .out(multiplexer_5_out), .sel(decoder_2_out0));
  assign or_10_out = {demultiplexer_2_out3, demultiplexer_2_out2, demultiplexer_2_out1, demultiplexer_2_out0} | {Task_row_4[0], Task_row_4[1], Task_row_4[2], Task_row_4[3], Task_row_4[4], Task_row_4[5], Task_row_4[6], Task_row_4[7], Task_row_3[0], Task_row_3[1], Task_row_3[2], Task_row_3[3], Task_row_3[4], Task_row_3[5], Task_row_3[6], Task_row_3[7], Task_row_2[0], Task_row_2[1], Task_row_2[2], Task_row_2[3], Task_row_2[4], Task_row_2[5], Task_row_2[6], Task_row_2[7], Task_row_1[0], Task_row_1[1], Task_row_1[2], Task_row_1[3], Task_row_1[4], Task_row_1[5], Task_row_1[6], Task_row_1[7]};  // OR_Gate or_10, 32 bits wide
  assign and_5_out = ~{demultiplexer_2_out3, demultiplexer_2_out2, demultiplexer_2_out1, demultiplexer_2_out0} & {Task_row_4[0], Task_row_4[1], Task_row_4[2], Task_row_4[3], Task_row_4[4], Task_row_4[5], Task_row_4[6], Task_row_4[7], Task_row_3[0], Task_row_3[1], Task_row_3[2], Task_row_3[3], Task_row_3[4], Task_row_3[5], Task_row_3[6], Task_row_3[7], Task_row_2[0], Task_row_2[1], Task_row_2[2], Task_row_2[3], Task_row_2[4], Task_row_2[5], Task_row_2[6], Task_row_2[7], Task_row_1[0], Task_row_1[1], Task_row_1[2], Task_row_1[3], Task_row_1[4], Task_row_1[5], Task_row_1[6], Task_row_1[7]};  // AND_Gate and_5, 32 bits wide
  assign and_6_out = ~{demultiplexer_3_out3, demultiplexer_3_out2, demultiplexer_3_out1, demultiplexer_3_out0} & {Task_row_8[0], Task_row_8[1], Task_row_8[2], Task_row_8[3], Task_row_8[4], Task_row_8[5], Task_row_8[6], Task_row_8[7], Task_row_7[0], Task_row_7[1], Task_row_7[2], Task_row_7[3], Task_row_7[4], Task_row_7[5], Task_row_7[6], Task_row_7[7], Task_row_6[0], Task_row_6[1], Task_row_6[2], Task_row_6[3], Task_row_6[4], Task_row_6[5], Task_row_6[6], Task_row_6[7], Task_row_5[0], Task_row_5[1], Task_row_5[2], Task_row_5[3], Task_row_5[4], Task_row_5[5], Task_row_5[6], Task_row_5[7]};  // AND_Gate and_6, 32 bits wide
  assign or_11_out = {demultiplexer_3_out3, demultiplexer_3_out2, demultiplexer_3_out1, demultiplexer_3_out0} | {Task_row_8[0], Task_row_8[1], Task_row_8[2], Task_row_8[3], Task_row_8[4], Task_row_8[5], Task_row_8[6], Task_row_8[7], Task_row_7[0], Task_row_7[1], Task_row_7[2], Task_row_7[3], Task_row_7[4], Task_row_7[5], Task_row_7[6], Task_row_7[7], Task_row_6[0], Task_row_6[1], Task_row_6[2], Task_row_6[3], Task_row_6[4], Task_row_6[5], Task_row_6[6], Task_row_6[7], Task_row_5[0], Task_row_5[1], Task_row_5[2], Task_row_5[3], Task_row_5[4], Task_row_5[5], Task_row_5[6], Task_row_5[7]};  // OR_Gate or_11, 32 bits wide
  Multiplexer #(.width(32), .enable("false")) multiplexer_6 (
    .in0(or_11_out), .in1(and_6_out), .out(multiplexer_6_out), .sel(decoder_2_out0));
  or or_12 (or_12_out, decoder_2_out0, decoder_2_out3);
  assign DataO_1 = decoder_2_out3 ? {Task_row_4[0], Task_row_4[1], Task_row_4[2], Task_row_4[3], Task_row_4[4], Task_row_4[5], Task_row_4[6], Task_row_4[7], Task_row_3[0], Task_row_3[1], Task_row_3[2], Task_row_3[3], Task_row_3[4], Task_row_3[5], Task_row_3[6], Task_row_3[7], Task_row_2[0], Task_row_2[1], Task_row_2[2], Task_row_2[3], Task_row_2[4], Task_row_2[5], Task_row_2[6], Task_row_2[7], Task_row_1[0], Task_row_1[1], Task_row_1[2], Task_row_1[3], Task_row_1[4], Task_row_1[5], Task_row_1[6], Task_row_1[7]} : 32'bz;  // Controlled_Buffer controlled_buffer_5
  Register #(.width(32)) register_5 (
    .D(multiplexer_5_out), .en(or_9_out),
    .Q({Task_row_4[0], Task_row_4[1], Task_row_4[2], Task_row_4[3], Task_row_4[4], Task_row_4[5], Task_row_4[6], Task_row_4[7], Task_row_3[0], Task_row_3[1], Task_row_3[2], Task_row_3[3], Task_row_3[4], Task_row_3[5], Task_row_3[6], Task_row_3[7], Task_row_2[0], Task_row_2[1], Task_row_2[2], Task_row_2[3], Task_row_2[4], Task_row_2[5], Task_row_2[6], Task_row_2[7], Task_row_1[0], Task_row_1[1], Task_row_1[2], Task_row_1[3], Task_row_1[4], Task_row_1[5], Task_row_1[6], Task_row_1[7]}),
    .clk(wr), .clr(RST));
  Register #(.width(32)) register_6 (
    .D(multiplexer_6_out), .en(or_12_out),
    .Q({Task_row_8[0], Task_row_8[1], Task_row_8[2], Task_row_8[3], Task_row_8[4], Task_row_8[5], Task_row_8[6], Task_row_8[7], Task_row_7[0], Task_row_7[1], Task_row_7[2], Task_row_7[3], Task_row_7[4], Task_row_7[5], Task_row_7[6], Task_row_7[7], Task_row_6[0], Task_row_6[1], Task_row_6[2], Task_row_6[3], Task_row_6[4], Task_row_6[5], Task_row_6[6], Task_row_6[7], Task_row_5[0], Task_row_5[1], Task_row_5[2], Task_row_5[3], Task_row_5[4], Task_row_5[5], Task_row_5[6], Task_row_5[7]}),
    .clk(wr), .clr(RST));
  assign DataO_2 = decoder_2_out3 ? {Task_row_8[0], Task_row_8[1], Task_row_8[2], Task_row_8[3], Task_row_8[4], Task_row_8[5], Task_row_8[6], Task_row_8[7], Task_row_7[0], Task_row_7[1], Task_row_7[2], Task_row_7[3], Task_row_7[4], Task_row_7[5], Task_row_7[6], Task_row_7[7], Task_row_6[0], Task_row_6[1], Task_row_6[2], Task_row_6[3], Task_row_6[4], Task_row_6[5], Task_row_6[6], Task_row_6[7], Task_row_5[0], Task_row_5[1], Task_row_5[2], Task_row_5[3], Task_row_5[4], Task_row_5[5], Task_row_5[6], Task_row_5[7]} : 32'bz;  // Controlled_Buffer controlled_buffer_6

  assign p2_row_1[8] = 1'b0;
  assign p2_row_2[8] = 1'b0;
  assign p2_row_3[8] = 1'b0;
  assign p2_row_4[8] = 1'b0;
  assign p2_row_5[8] = 1'b0;
  assign p2_row_6[8] = 1'b0;
  assign p2_row_7[8] = 1'b0;
  assign p2_row_8[8] = 1'b0;
  assign Task_row_1[9:8] = 2'b00;
  assign Task_row_2[9:8] = 2'b00;
  assign Task_row_3[9:8] = 2'b00;
  assign Task_row_4[9:8] = 2'b00;
  assign Task_row_5[9:8] = 2'b00;
  assign Task_row_6[9:8] = 2'b00;
  assign Task_row_7[9:8] = 2'b00;
  assign Task_row_8[9:8] = 2'b00;
endmodule

module pointer_mover (
  input  [4:0] KBD_command,
  input  CLK,
  input  RST,
  output [7:0] CSC,
  output [7:0] CSR
);

  wire and_1_out, and_2_out, and_3_out, and_4_out, comparator_1_eq, comparator_2_eq, comparator_3_eq,
       comparator_4_eq, not_1_out, not_2_out, or_1_out, or_2_out, or_3_out, or_4_out;
  wire [7:0] multiplexer_1_out, multiplexer_2_out, multiplexer_3_out, multiplexer_4_out;

  // Probe on KBD_command
  Comparator #(.width(5), .mode("unsigned")) comparator_1 (
    .a(KBD_command), .b(5'b10001), .eq(comparator_1_eq));  // open: gt, lt
  Comparator #(.width(5), .mode("unsigned")) comparator_2 (
    .a(KBD_command), .b(5'b10010), .eq(comparator_2_eq));  // open: gt, lt
  Comparator #(.width(5), .mode("unsigned")) comparator_3 (
    .a(KBD_command), .b(5'b10000), .eq(comparator_3_eq));  // open: gt, lt
  Comparator #(.width(5), .mode("unsigned")) comparator_4 (
    .a(KBD_command), .b(5'b10011), .eq(comparator_4_eq));  // open: gt, lt
  or or_1 (or_1_out, comparator_1_eq, comparator_2_eq);
  or or_2 (or_2_out, comparator_3_eq, comparator_4_eq);
  Multiplexer #(.width(8), .enable("false")) multiplexer_1 (
    .in0({CSC[0], CSC[7:1]}), .in1({CSC[6:0], CSC[7]}), .out(multiplexer_1_out), .sel(comparator_1_eq));
  Multiplexer #(.width(8), .enable("false")) multiplexer_2 (
    .in0({CSR[0], CSR[7:1]}), .in1({CSR[6:0], CSR[7]}), .out(multiplexer_2_out), .sel(comparator_3_eq));
  Multiplexer #(.width(8), .enable("false")) multiplexer_3 (
    .in0(multiplexer_1_out), .in1(8'h1), .out(multiplexer_3_out), .sel(RST));
  Register register_1 (.D(multiplexer_3_out), .en(1'b1), .Q(CSC), .clk(or_3_out), .clr(1'b0));
  or or_3 (or_3_out, and_3_out, and_1_out);
  and and_1 (and_1_out, CLK, or_1_out);
  Multiplexer #(.width(8), .enable("false")) multiplexer_4 (
    .in0(multiplexer_2_out), .in1(8'h1), .out(multiplexer_4_out), .sel(RST));
  Register register_2 (.D(multiplexer_4_out), .en(1'b1), .Q(CSR), .clk(or_4_out), .clr(1'b0));
  or or_4 (or_4_out, and_4_out, and_2_out);
  and and_2 (and_2_out, CLK, or_2_out);
  and and_3 (and_3_out, ~RST, ~not_1_out);  // AND_Gate
  not not_1 (not_1_out, RST);
  and and_4 (and_4_out, ~RST, ~not_2_out);  // AND_Gate
  not not_2 (not_2_out, RST);
endmodule

module pointer_controller (
  input  Active,
  input  [4:0] KBD_command,
  input  CLK,
  input  RST,
  input  [31:0] Field_state_1,
  input  [31:0] Field_state_2,
  input  Allow_nearby,
  input  Free_mode,
  output [7:0] CSC,
  output [7:0] CSR,
  output Err,
  output Ready
);

  wire and_3_out, and_4_out, clk_t, counter_1_carry, d_ff_1_q, not_1_out, not_2_out, or_1_out, or_2_out,
       or_3_out, or_4_out, or_5_out, stop, xor_1_out;
  wire [3:0] counter_1_q;
  wire [7:0] and_2_out, controlled_buffer_1_out;

  and and_1 (clk_t, ~stop, Active, CLK);  // AND_Gate
  assign controlled_buffer_1_out = CSR[0] ? Field_state_1[7:0] : 8'bz;  // Controlled_Buffer controlled_buffer_1
  pointer_mover pointer_mover_1 (.CLK(clk_t), .RST(RST), .CSC(CSC), .CSR(CSR), .KBD_command(KBD_command));
  assign controlled_buffer_1_out = CSR[1] ? Field_state_1[15:8] : 8'bz;  // Controlled_Buffer controlled_buffer_2
  assign controlled_buffer_1_out = CSR[2] ? Field_state_1[23:16] : 8'bz;  // Controlled_Buffer controlled_buffer_3
  assign controlled_buffer_1_out = CSR[3] ? Field_state_1[31:24] : 8'bz;  // Controlled_Buffer controlled_buffer_4
  assign controlled_buffer_1_out = CSR[4] ? Field_state_2[7:0] : 8'bz;  // Controlled_Buffer controlled_buffer_5
  assign controlled_buffer_1_out = CSR[5] ? Field_state_2[15:8] : 8'bz;  // Controlled_Buffer controlled_buffer_6
  assign controlled_buffer_1_out = CSR[6] ? Field_state_2[23:16] : 8'bz;  // Controlled_Buffer controlled_buffer_7
  assign controlled_buffer_1_out = CSR[7] ? Field_state_2[31:24] : 8'bz;  // Controlled_Buffer controlled_buffer_8
  assign and_2_out = CSC & controlled_buffer_1_out;  // AND_Gate and_2, 8 bits wide
  or or_1 (or_1_out, and_2_out[0], and_2_out[1], and_2_out[2], and_2_out[3], and_2_out[4], and_2_out[5], and_2_out[6], and_2_out[7], 1'b0);
  D_Flip_Flop d_ff_1 (
    .clk(Active), .D(or_1_out), .Q(d_ff_1_q), .en(Allow_nearby), .reset(or_2_out));  // open: Qn, preset
  and and_3 (and_3_out, Allow_nearby, d_ff_1_q);
  or or_2 (or_2_out, RST, and_4_out);
  and and_4 (and_4_out, ~Active, ~not_1_out);  // AND_Gate
  Counter #(.width(4), .max('h8), .trigger("falling")) counter_1 (
    .load(1'b0), .count(1'b1), .Q(counter_1_q), .carry(counter_1_carry), .clk(clk_t), .clr(or_3_out));  // open: D
  or or_3 (or_3_out, RST, xor_1_out);
  not not_1 (not_1_out, Active);
  or or_4 (or_4_out, 1'b0, counter_1_q[0], counter_1_q[1], counter_1_q[2], counter_1_q[3]);
  xor xor_1 (xor_1_out, ~Active, not_2_out);  // XOR_Gate
  not not_2 (not_2_out, Active);
  or or_5 (or_5_out, and_3_out, or_1_out, Free_mode);
  and and_5 (Err, counter_1_carry, ~Ready);  // AND_Gate
  or or_6 (stop, Err, Ready);
  and and_6 (Ready, or_4_out, or_5_out);
endmodule
