// Logisim project cell controller.circ as structural Verilog: 3 circuits, main circuit Cell controller
module Cell_controller (
  input  CSR,
  input  [11:0] in_2,
  input  CSC,
  input  [1:0] SPI,
  input  [11:0] in_5,
  input  [11:0] in_6,
  input  [11:0] in_7,
  output [11:0] out_8,
  output MISO,
  output [11:0] out_10,
  output [11:0] out_11,
  output [11:0] out_12,
  output [4:0] out_13,
  output [4:0] out_14,
  output [4:0] out_15,
  output [4:0] out_16,
  output [4:0] out_17,
  output [4:0] out_18,
  output [4:0] out_19,
  output [4:0] out_20,
  output [4:0] out_21,
  output [4:0] out_22,
  output [4:0] out_23,
  output [7:0] out_24,
  output [7:0] out_25,
  output [7:0] out_26,
  output [7:0] out_27,
  output [7:0] out_28,
  output [7:0] out_29,
  output [7:0] out_30,
  output [7:0] out_31,
  output [7:0] out_32,
  output [7:0] out_33,
  output [7:0] out_34,
  output [7:0] out_35,
  output [7:0] out_36,
  output [7:0] out_37,
  output [7:0] out_38,
  output [7:0] out_39,
  output [7:0] out_40,
  output [7:0] out_41,
  output [7:0] out_42,
  output [7:0] out_43,
  output [7:0] out_44,
  output [7:0] out_45
);

  wire and_1_out, and_4_out, and_5_out, and_6_out, command_decoder_1_is_energy, command_decoder_1_is_player,
       command_decoder_1_is_type, command_decoder_1_is_write, Err, or_1_out, or_3_out, reg_update,
       spi_module_cell_1_clk_out, spi_module_cell_1_input_transanction_end, spi_module_cell_1_task_conf,
       task_update;
  wire [1:0] display_player, input_player, input_type, or_2_out, spi_module_cell_1_is_task, type_reg_q,
       type_reg_q_2;
  wire [3:0] display_task_type;
  wire [4:0] spi_module_cell_1_command;
  wire [9:0] display_energy;
  wire [10:0] adder_1_out, input_energy;

  and and_1 (and_1_out, CSR, CSC);
  SPI_module__cell spi_module_cell_1 (
    .CS(and_1_out), .CLK(SPI[0]), .MOSI(SPI[1]), .err(Err), .energy_in({1'b0, display_energy}),
    .clk_out(spi_module_cell_1_clk_out), .is_task(spi_module_cell_1_is_task),
    .task_conf(spi_module_cell_1_task_conf), .command(spi_module_cell_1_command), .energy_out(input_energy),
    .input_transanction_end(spi_module_cell_1_input_transanction_end), .type_select_out(input_type),
    .player_select_out(input_player), .MISO(MISO));  // open: type_select_in, player_select_in, is_selected, move_end_1, move_end_2, output_transanction_end, is_player_2
  and and_2 (reg_update, ~spi_module_cell_1_clk_out, spi_module_cell_1_input_transanction_end);  // AND_Gate
  and and_3 (task_update, ~spi_module_cell_1_clk_out, spi_module_cell_1_task_conf);  // AND_Gate
  command_decoder command_decoder_1 (
    .Command_in(spi_module_cell_1_command), .is_energy(command_decoder_1_is_energy),
    .is_type(command_decoder_1_is_type), .is_player(command_decoder_1_is_player),
    .is_write(command_decoder_1_is_write));  // open: direction, is_direction, is_task, is_clear, is_reset
  or or_1 (or_1_out, spi_module_cell_1_is_task[0], command_decoder_1_is_type, spi_module_cell_1_is_task[1]);
  Adder #(.width(11)) adder_1 (.a({1'b0, display_energy}), .b(input_energy), .out(adder_1_out));  // open: cin, cout
  and and_4 (and_4_out, command_decoder_1_is_energy, command_decoder_1_is_write, reg_update);
  assign or_2_out = spi_module_cell_1_is_task | type_reg_q_2;  // OR_Gate or_2, 2 bits wide
  and and_5 (and_5_out, or_1_out, or_3_out);
  or or_3 (or_3_out, reg_update, task_update);
  and and_6 (and_6_out, command_decoder_1_is_player, command_decoder_1_is_write, reg_update);
  Register #(.width(10)) Energy_reg (
    .D(adder_1_out[9:0]), .Q(display_energy), .clk(and_4_out), .clr(1'b0));  // open: en
  Register #(.width(4)) type_reg (
    .D({or_2_out, input_type}), .Q({type_reg_q_2, type_reg_q}), .clk(and_5_out), .clr(1'b0));  // open: en
  Register #(.width(2)) player_reg (.D(input_player), .Q(display_player), .clk(and_6_out), .clr(1'b0));  // open: en
  assign display_task_type = {spi_module_cell_1_is_task, 2'b00} | {type_reg_q_2, type_reg_q};  // OR_Gate or_4, 4 bits wide
  DotMatrix #(.matrixcols(11), .matrixrows(8)) dotmatrix_1 (
    .col0(out_24), .col1(out_25), .col2(out_26), .col3(out_27), .col4(out_28), .col5(out_29), .col6(out_30),
    .col7(out_31), .col8(out_32), .col9(out_33), .col10(out_34));
  // Чья_Тип чья_тип_1: pin names not known; wires that end beside it: display_player, display_task_type, out_24, out_25, out_26, out_27, out_28, out_29, out_30, out_31, out_32, out_33, out_34, out_35, out_36, out_37, out_38, out_39, out_40, out_41, out_42, out_43, out_44, out_45
  DotMatrix #(.matrixcols(11), .matrixrows(8)) dotmatrix_2 (
    .col0(out_35), .col1(out_36), .col2(out_37), .col3(out_38), .col4(out_39), .col5(out_40), .col6(out_41),
    .col7(out_42), .col8(out_43), .col9(out_44), .col10(out_45));
  DotMatrix #(.matrixcols(11), .matrixrows(5)) dotmatrix_3 (
    .col0(out_13), .col1(out_14), .col2(out_15), .col3(out_16), .col4(out_17), .col5(out_18), .col6(out_19),
    .col7(out_20), .col8(out_21), .col9(out_22), .col10(out_23));
  // Цифры цифры_1: pin names not known; wires that end beside it: display_energy, out_13, out_14, out_15, out_16, out_17, out_18, out_19, out_20, out_21, out_22, out_23

  // Other names for the same wires on the sheet: E1[4:0] = out_13; E2[4:0] = out_14; E3[4:0] = out_15;
  //   E4[4:0] = out_16; E5[4:0] = out_17; E6[4:0] = out_18; E7[4:0] = out_19; E8[4:0] = out_20; E9[4:0] = out_21;
  //   E10[4:0] = out_22; E11[4:0] = out_23; О1[7:0] = out_24; О2[7:0] = out_25; О3[7:0] = out_26; О4[7:0] = out_27;
  //   О5[7:0] = out_28; О6[7:0] = out_29; О7[7:0] = out_30; О8[7:0] = out_31; О9[7:0] = out_32; О10[7:0] = out_33;
  //   О11[7:0] = out_34; С1[7:0] = out_35; С2[7:0] = out_36; С3[7:0] = out_37; С4[7:0] = out_38; С5[7:0] = out_39;
  //   С6[7:0] = out_40; С7[7:0] = out_41; С8[7:0] = out_42; С9[7:0] = out_43; С10[7:0] = out_44; С11[7:0] = out_45

  // Notes on the sheet:
  //   CSC: pull=down
  //   SPI: pull=down
  //   CSR: pull=down
  //   Number mtx output
  //   Orange mtx output
  //   Blue mtx output
endmodule

module local_test (
  input  [4:0] in_1,
  input  [10:0] in_2,
  input  in_3,
  input  in_4,
  input  [7:0] in_5,
  input  in_6
);

  wire clock_1_out, pull_resistor_1_node, spi_module_master_1_communication_end,
       spi_module_master_1_input_transanction_end, spi_module_master_1_output_transanction_end;
  wire [1:0] spi_module_master_1_clk;
  wire [4:0] cell_controller_1_out_13, cell_controller_1_out_14, cell_controller_1_out_15,
       cell_controller_1_out_16, cell_controller_1_out_17, cell_controller_1_out_18,
       cell_controller_1_out_19, cell_controller_1_out_20, cell_controller_1_out_21,
       cell_controller_1_out_22, cell_controller_1_out_23, cell_controller_2_out_13,
       cell_controller_2_out_14, cell_controller_2_out_15, cell_controller_2_out_16,
       cell_controller_2_out_17, cell_controller_2_out_18, cell_controller_2_out_19,
       cell_controller_2_out_20, cell_controller_2_out_21, cell_controller_2_out_22, cell_controller_2_out_23;
  wire [7:0] cell_controller_1_out_24, cell_controller_1_out_25, cell_controller_1_out_26,
       cell_controller_1_out_27, cell_controller_1_out_28, cell_controller_1_out_29,
       cell_controller_1_out_30, cell_controller_1_out_31, cell_controller_1_out_32,
       cell_controller_1_out_33, cell_controller_1_out_34, cell_controller_1_out_35,
       cell_controller_1_out_36, cell_controller_1_out_37, cell_controller_1_out_38,
       cell_controller_1_out_39, cell_controller_1_out_40, cell_controller_1_out_41,
       cell_controller_1_out_42, cell_controller_1_out_43, cell_controller_1_out_44,
       cell_controller_1_out_45, cell_controller_2_out_24, cell_controller_2_out_25,
       cell_controller_2_out_26, cell_controller_2_out_27, cell_controller_2_out_28,
       cell_controller_2_out_29, cell_controller_2_out_30, cell_controller_2_out_31,
       cell_controller_2_out_32, cell_controller_2_out_33, cell_controller_2_out_34,
       cell_controller_2_out_35, cell_controller_2_out_36, cell_controller_2_out_37,
       cell_controller_2_out_38, cell_controller_2_out_39, cell_controller_2_out_40,
       cell_controller_2_out_41, cell_controller_2_out_42, cell_controller_2_out_43,
       cell_controller_2_out_44, cell_controller_2_out_45;
  wire [15:0] spi_module_master_1_recv_data;

  Clock clock_1 (.out(clock_1_out));
  LED led_1 (.in(spi_module_master_1_communication_end));
  LED led_2 (.in(spi_module_master_1_input_transanction_end));
  LED led_3 (.in(spi_module_master_1_output_transanction_end));
  // Probe on spi_module_master_1_recv_data
  SPI_module__master spi_module_master_1 (
    .In_clock(clock_1_out), .MISO(pull_resistor_1_node), .CLK(spi_module_master_1_clk[0]),
    .MOSI(spi_module_master_1_clk[1]), .Output_transanction_end(spi_module_master_1_output_transanction_end),
    .Input_transanction_end(spi_module_master_1_input_transanction_end), .Control_command(in_5),
    .Send_command(in_1), .Send_energy(in_2), .Recv_data(spi_module_master_1_recv_data),
    .Communication_end(spi_module_master_1_communication_end));
  Pull_Resistor pull_resistor_1 (.node(pull_resistor_1_node));
  // Probe on spi_module_master_1_clk
  DotMatrix #(.matrixcols(11), .matrixrows(5)) dotmatrix_1 (
    .col0(cell_controller_1_out_13), .col1(cell_controller_1_out_14), .col2(cell_controller_1_out_15),
    .col3(cell_controller_1_out_16), .col4(cell_controller_1_out_17), .col5(cell_controller_1_out_18),
    .col6(cell_controller_1_out_19), .col7(cell_controller_1_out_20), .col8(cell_controller_1_out_21),
    .col9(cell_controller_1_out_22), .col10(cell_controller_1_out_23));
  Cell_controller cell_controller_1 (
    .out_13(cell_controller_1_out_13), .out_24(cell_controller_1_out_24), .out_14(cell_controller_1_out_14),
    .out_35(cell_controller_1_out_35), .out_25(cell_controller_1_out_25), .out_15(cell_controller_1_out_15),
    .out_36(cell_controller_1_out_36), .out_26(cell_controller_1_out_26), .out_16(cell_controller_1_out_16),
    .out_37(cell_controller_1_out_37), .out_17(cell_controller_1_out_17), .out_27(cell_controller_1_out_27),
    .out_38(cell_controller_1_out_38), .out_18(cell_controller_1_out_18), .out_28(cell_controller_1_out_28),
    .out_19(cell_controller_1_out_19), .out_39(cell_controller_1_out_39), .out_29(cell_controller_1_out_29),
    .out_20(cell_controller_1_out_20), .out_40(cell_controller_1_out_40), .out_30(cell_controller_1_out_30),
    .out_21(cell_controller_1_out_21), .out_41(cell_controller_1_out_41), .out_22(cell_controller_1_out_22),
    .out_31(cell_controller_1_out_31), .out_42(cell_controller_1_out_42), .out_23(cell_controller_1_out_23),
    .out_32(cell_controller_1_out_32), .out_43(cell_controller_1_out_43), .out_33(cell_controller_1_out_33),
    .out_44(cell_controller_1_out_44), .out_34(cell_controller_1_out_34), .out_45(cell_controller_1_out_45),
    .CSC(in_4), .CSR(in_6), .MISO(pull_resistor_1_node), .SPI(spi_module_master_1_clk));  // open: in_5, out_11, in_2, out_8, in_6, out_10, in_7, out_12
  DotMatrix #(.matrixcols(11), .matrixrows(8)) dotmatrix_2 (
    .col0(cell_controller_1_out_24), .col1(cell_controller_1_out_25), .col2(cell_controller_1_out_26),
    .col3(cell_controller_1_out_27), .col4(cell_controller_1_out_28), .col5(cell_controller_1_out_29),
    .col6(cell_controller_1_out_30), .col7(cell_controller_1_out_31), .col8(cell_controller_1_out_32),
    .col9(cell_controller_1_out_33), .col10(cell_controller_1_out_34));
  DotMatrix #(.matrixcols(11), .matrixrows(8)) dotmatrix_3 (
    .col0(cell_controller_1_out_35), .col1(cell_controller_1_out_36), .col2(cell_controller_1_out_37),
    .col3(cell_controller_1_out_38), .col4(cell_controller_1_out_39), .col5(cell_controller_1_out_40),
    .col6(cell_controller_1_out_41), .col7(cell_controller_1_out_42), .col8(cell_controller_1_out_43),
    .col9(cell_controller_1_out_44), .col10(cell_controller_1_out_45));
  Cell_controller cell_controller_2 (
    .out_13(cell_controller_2_out_13), .out_24(cell_controller_2_out_24), .out_14(cell_controller_2_out_14),
    .out_35(cell_controller_2_out_35), .out_25(cell_controller_2_out_25), .out_15(cell_controller_2_out_15),
    .out_36(cell_controller_2_out_36), .out_26(cell_controller_2_out_26), .out_16(cell_controller_2_out_16),
    .out_37(cell_controller_2_out_37), .out_17(cell_controller_2_out_17), .out_27(cell_controller_2_out_27),
    .out_38(cell_controller_2_out_38), .out_18(cell_controller_2_out_18), .out_28(cell_controller_2_out_28),
    .out_19(cell_controller_2_out_19), .out_39(cell_controller_2_out_39), .out_29(cell_controller_2_out_29),
    .out_20(cell_controller_2_out_20), .out_40(cell_controller_2_out_40), .out_30(cell_controller_2_out_30),
    .out_21(cell_controller_2_out_21), .out_41(cell_controller_2_out_41), .out_22(cell_controller_2_out_22),
    .out_31(cell_controller_2_out_31), .out_42(cell_controller_2_out_42), .out_23(cell_controller_2_out_23),
    .out_32(cell_controller_2_out_32), .out_43(cell_controller_2_out_43), .out_33(cell_controller_2_out_33),
    .out_44(cell_controller_2_out_44), .out_34(cell_controller_2_out_34), .out_45(cell_controller_2_out_45),
    .CSC(in_3), .CSR(in_6), .MISO(pull_resistor_1_node), .SPI(spi_module_master_1_clk));  // open: in_5, out_11, in_2, out_8, in_6, out_10, in_7, out_12
  DotMatrix #(.matrixcols(11), .matrixrows(5)) dotmatrix_4 (
    .col0(cell_controller_2_out_13), .col1(cell_controller_2_out_14), .col2(cell_controller_2_out_15),
    .col3(cell_controller_2_out_16), .col4(cell_controller_2_out_17), .col5(cell_controller_2_out_18),
    .col6(cell_controller_2_out_19), .col7(cell_controller_2_out_20), .col8(cell_controller_2_out_21),
    .col9(cell_controller_2_out_22), .col10(cell_controller_2_out_23));
  DotMatrix #(.matrixcols(11), .matrixrows(8)) dotmatrix_5 (
    .col0(cell_controller_2_out_24), .col1(cell_controller_2_out_25), .col2(cell_controller_2_out_26),
    .col3(cell_controller_2_out_27), .col4(cell_controller_2_out_28), .col5(cell_controller_2_out_29),
    .col6(cell_controller_2_out_30), .col7(cell_controller_2_out_31), .col8(cell_controller_2_out_32),
    .col9(cell_controller_2_out_33), .col10(cell_controller_2_out_34));
  DotMatrix #(.matrixcols(11), .matrixrows(8)) dotmatrix_6 (
    .col0(cell_controller_2_out_35), .col1(cell_controller_2_out_36), .col2(cell_controller_2_out_37),
    .col3(cell_controller_2_out_38), .col4(cell_controller_2_out_39), .col5(cell_controller_2_out_40),
    .col6(cell_controller_2_out_41), .col7(cell_controller_2_out_42), .col8(cell_controller_2_out_43),
    .col9(cell_controller_2_out_44), .col10(cell_controller_2_out_45));

  // Notes on the sheet:
  //   in_4: pull=down
  //   in_3: pull=down
  //   in_6: pull=down
endmodule

module \РЕГИСТРЫ_Тип  (
  input  [1:0] Type,
  input  [1:0] Task,
  input  Conf,
  input  [1:0] Player,
  input  in_5,
  output [3:0] out_6,
  output Err,
  output [1:0] For_paint,
  output [1:0] out_9
);

  wire and_1_out, and_2_out;
  wire [1:0] undriven;

  Multiplexer #(.width(2), .enable("false")) multiplexer_1 (.in0(2'b00), .in1(Player), .out(out_9), .sel(in_5));
  Multiplexer #(.width(2), .enable("false")) multiplexer_2 (.in0(2'b00), .in1(Task), .out(out_6[3:2]), .sel(Conf));
  buf and_1 (and_1_out, out_6[3]);  // AND_Gate
  buf and_2 (and_2_out, out_6[2]);  // AND_Gate
  Multiplexer #(.width(2), .enable("false")) multiplexer_3 (.in0(undriven), .in1(Task));  // open: out, sel
  or or_1 (Err, and_1_out, and_2_out);

  assign out_6[1:0] = Type;

  // Notes on the sheet:
  //   игнорируем
  //   ITE
endmodule
