// Logisim project o_math_i_math.circ as structural Verilog: 3 circuits, main circuit O_math
module O_math (
  input  [9:0] Energy,
  input  [9:0] C_reg,
  input  Cancel_transfer,
  input  [10:0] mv_energy,
  output [9:0] Energy_2,
  output [9:0] C_reg_2,
  output err
);

  wire comparator_1_eq, comparator_1_gt, comparator_2_lt, comparator_3_gt, comparator_4_lt, comparator_5_lt,
       not_1_out, not_2_out, or_1_out, pull_resistor_1_node;
  wire [9:0] adder_3_out, adder_4_out, multiplexer_2_out, multiplexer_3_out, multiplexer_4_out,
       multiplexer_5_out, multiplexer_6_out, multiplexer_7_out, multiplexer_8_out, subtractor_5_out,
       subtractor_6_out;
  wire [10:0] adder_1_out, adder_2_out, multiplexer_1_out, subtractor_1_out, subtractor_2_out,
       subtractor_3_out, subtractor_4_out;
  wire [10:10] adder_3_out_2, adder_4_out_2, subtractor_5_out_2, subtractor_6_out_2;

  // Probe on adder_1_out
  // Probe on mv_energy
  // Probe on {1'b0, C_reg}
  // Probe on {1'b0, C_reg}
  // Probe on {1'b0, Energy}
  Subtractor #(.width(11)) subtractor_1 (.a({1'b0, C_reg}), .b(mv_energy), .out(subtractor_1_out));  // open: bin, bout
  Adder #(.width(11)) adder_1 (.a({1'b0, Energy}), .b({1'b0, C_reg}), .out(adder_1_out));  // open: cin, cout
  Subtractor #(.width(11)) subtractor_2 (.a({1'b0, Energy}), .b(mv_energy), .out(subtractor_2_out));  // open: bin, bout
  // Probe on subtractor_2_out
  Comparator #(.width(11)) comparator_1 (
    .a({1'b0, Energy}), .b(mv_energy), .gt(comparator_1_gt), .eq(comparator_1_eq));  // open: lt
  Comparator #(.width(11)) comparator_2 (.a(mv_energy), .b(11'h3e7), .lt(comparator_2_lt));  // open: gt, eq
  // Probe on subtractor_1_out
  Comparator #(.width(11), .mode("unsigned")) comparator_3 (
    .a(adder_1_out), .b(11'h3e7), .gt(comparator_3_gt));  // open: eq, lt
  or or_1 (or_1_out, comparator_1_gt, comparator_1_eq);
  Comparator #(.width(11)) comparator_4 (.a(mv_energy), .b(11'h419), .lt(comparator_4_lt));  // open: gt, eq
  Adder #(.width(11)) adder_2 (.a(mv_energy), .b({1'b0, C_reg}), .out(adder_2_out));  // open: cin, cout
  // Probe on {1'b0, Energy}
  Multiplexer #(.width(11), .enable("false")) multiplexer_1 (
    .in0(adder_1_out), .in1(11'h3e7), .out(multiplexer_1_out), .sel(comparator_3_gt));
  Subtractor #(.width(11)) subtractor_3 (
    .a({1'b0, Energy}), .b(subtractor_2_out), .out(subtractor_3_out));  // open: bin, bout
  // Probe on adder_2_out
  Subtractor #(.width(11)) subtractor_4 (
    .a({1'b0, C_reg}), .b(subtractor_1_out), .out(subtractor_4_out));  // open: bin, bout
  // Probe on subtractor_4_out
  // Probe on subtractor_3_out
  Subtractor #(.width(11)) subtractor_5 (
    .a({1'b0, Energy}), .b(subtractor_3_out), .out({subtractor_5_out_2[10], subtractor_5_out}));  // open: bin, bout
  Adder #(.width(11)) adder_3 (
    .a({1'b0, C_reg}), .b(subtractor_3_out), .out({adder_3_out_2[10], adder_3_out}));  // open: cin, cout
  // Probe on {adder_3_out_2[10], adder_3_out}
  not not_1 (not_1_out, or_1_out);
  Pull_Resistor pull_resistor_1 (.node(pull_resistor_1_node));
  Transistor #(.\type ("n")) transistor_1 (.in(adder_2_out[10]), .out(pull_resistor_1_node), .gate(mv_energy[10]));
  Adder #(.width(11)) adder_4 (
    .a({1'b0, C_reg}), .b(subtractor_4_out), .out({adder_4_out_2[10], adder_4_out}));  // open: cin, cout
  Subtractor #(.width(11)) subtractor_6 (
    .a({1'b0, Energy}), .b(subtractor_4_out), .out({subtractor_6_out_2[10], subtractor_6_out}));  // open: bin, bout
  // Probe on {subtractor_6_out_2[10], subtractor_6_out}
  not not_2 (not_2_out, comparator_2_lt);
  // Probe on adder_4_out
  or or_2 (err, not_1_out, comparator_4_lt, pull_resistor_1_node, not_2_out);
  Multiplexer #(.width(10), .enable("false")) multiplexer_2 (
    .in0(adder_3_out), .in1(10'h3e7), .out(multiplexer_2_out), .sel(adder_3_out_2[10]));
  Multiplexer #(.width(10), .enable("false")) multiplexer_3 (
    .in0(adder_4_out), .in1(10'h3e7), .out(multiplexer_3_out), .sel(adder_4_out_2[10]));
  Comparator #(.width(11), .mode("unsigned")) comparator_5 (
    .a({subtractor_6_out_2[10], subtractor_6_out}), .b(11'h3e7), .lt(comparator_5_lt));  // open: gt, eq
  // Probe on multiplexer_4_out
  Multiplexer #(.width(10), .enable("false")) multiplexer_4 (
    .in0(10'h3e7), .in1(subtractor_6_out), .out(multiplexer_4_out), .sel(comparator_5_lt));
  // Probe on multiplexer_2_out
  Multiplexer #(.width(10), .enable("false")) multiplexer_5 (
    .in0(subtractor_5_out), .in1(multiplexer_4_out), .out(multiplexer_5_out), .sel(mv_energy[10]));
  Multiplexer #(.width(10), .enable("false")) multiplexer_6 (
    .in0(multiplexer_2_out), .in1(multiplexer_3_out), .out(multiplexer_6_out), .sel(mv_energy[10]));
  Multiplexer #(.width(10), .enable("false")) multiplexer_7 (
    .in0(multiplexer_5_out), .in1(Energy), .out(multiplexer_7_out), .sel(err));
  // Probe on multiplexer_6_out
  Multiplexer #(.width(10), .enable("false")) multiplexer_8 (
    .in0(multiplexer_6_out), .in1(C_reg), .out(multiplexer_8_out), .sel(err));
  Multiplexer #(.width(10), .enable("false")) multiplexer_9 (
    .in0(multiplexer_8_out), .in1({10{1'b0}}), .out(C_reg_2), .sel(Cancel_transfer));
  Multiplexer #(.width(10), .enable("false")) multiplexer_10 (
    .in0(multiplexer_7_out), .in1(multiplexer_1_out[9:0]), .out(Energy_2), .sel(Cancel_transfer));
  // Probe on C_reg_2
  // Probe on Energy_2
endmodule

module I_math (
  input  [11:0] Dl_1,
  input  [9:0] Energy,
  input  [1:0] player_select,
  input  [3:0] type_select,
  input  [11:0] Dl_4,
  input  [11:0] Dl_3,
  input  [11:0] Dl_2,
  output [9:0] Energy_2,
  output [1:0] player_select_2,
  output err
);
endmodule

module sum (
  input  [11:0] in_1,
  input  [11:0] in_2,
  output [9:0] out_3
);

  wire comparator_1_eq;
  wire [9:0] adder_1_out, subtractor_1_out;

  // Probe on in_2[9:0]
  // Probe on in_1[9:0]
  // Probe on in_2[11:10]
  // Probe on in_1[11:10]
  Adder #(.width(10)) adder_1 (.a(in_1[9:0]), .b(in_2[9:0]), .out(adder_1_out));  // open: cin, cout
  Subtractor #(.width(10)) subtractor_1 (.a(in_1[9:0]), .b(in_2[9:0]), .out(subtractor_1_out));  // open: bin, bout
  Comparator #(.width(2), .mode("unsigned")) comparator_1 (
    .a(in_1[11:10]), .b(in_2[11:10]), .eq(comparator_1_eq));  // open: gt, lt
  Multiplexer #(.width(10), .enable("false")) multiplexer_1 (
    .in0(subtractor_1_out), .in1(adder_1_out), .out(out_3), .sel(comparator_1_eq));
  // Probe on out_3
endmodule
